# Fritzing sketch circuit (saved by Fritzing 0.9.2b)
breadboards: 1

parts:
  Pre-Assembled_Female_BNC = Pre-Assembled Female BNC
  Conductivity_Circuit = Conductivity Circuit
  U1 = RF-LINK_TX [package=rf-link_tx]
  R3 = Resistor [tolerance=±5% resistance=220 package="2010 [SMD]"]
  LED1 = smd LED [color="Red (633nm)" package="0603 [SMD]"]
  R2 = Resistor [tolerance=±5% resistance=220 package="2010 [SMD]"]
  R1 = Resistor [tolerance=±5% resistance=220 package="2010 [SMD]"]
  Raspberry_Pi1 = Raspberry Pi B rev2
  R4 = Resistor [tolerance=±5% resistance=4.7k package="2010 [SMD]"]
  part = TEMPERATURE-SENSOR [package=to-92]
  part_2 = TEMPERATURE-SENSOR [package=to-92]

nets:
  VCC: Pre-Assembled_Female_BNC.NC, Conductivity_Circuit.Vcc, R1.Pin_1, Raspberry_Pi1.3V3, R4.Pin_0, part.VCC, part_2.VCC
  N1: Pre-Assembled_Female_BNC.PRB, Conductivity_Circuit.PRB
  N2: Pre-Assembled_Female_BNC.GND, Conductivity_Circuit.GND#5
  GND: Conductivity_Circuit.GND#0, U1.GND, Raspberry_Pi1.GND, part.GND, part_2.GND
  N3: Conductivity_Circuit.TX, R2.Pin_0, Raspberry_Pi1.GPIO_14
  N4: Conductivity_Circuit.RX, R1.Pin_0, Raspberry_Pi1.GPIO_15
  N5: U1.DATA, LED1.cathode
  +5V: U1.+5V, Raspberry_Pi1.5V
  N6: R3.Pin_0, LED1.anode
  N7: R3.Pin_1, Raspberry_Pi1.GPIO_7
  N8: Raspberry_Pi1.GPIO_4, R4.Pin_1, part.ADJ, part_2.ADJ
